# Fritzing sketch basic_node (saved by Fritzing 0.9.9b)

parts:
  D1ML1 = WeMos D1 Mini Lite [part_number="WeMos D1 Mini Lite"]
  BAT1 = 18650 battery holder [package=battery-18650-kit]
  Part5 = Adafruit ADS1115 16Bit I2C ADC [part_number=ADS1115]
  R5 = Resistor [tolerance=±5% resistance=36k power=0.25 package=THT]
  R6 = Resistor [tolerance=±5% resistance=100k power=0.25 package=THT]
  MCP1700 = Voltage Regulator [package=to-92]
  C3 = Electrolytic Capacitor [capacitance=100μF voltage=6.3V package="100 mil [THT, electrolytic]"]
  C2 = Electrolytic Capacitor [capacitance=1µF voltage=6.3V package="100 mil [THT, electrolytic]"]
  TP4056 = TP4056 [chip_label=TP4056 package="DIP (Dual Inline) [THT]"]
  R4 = Resistor [tolerance=±5% power=0.25 resistance=330 package=THT]
  LED2 = LED - 3mm [color="Green (565nm)" current=0.030 package="3 mm [THT]"]
  U1 = SWITCH_SPDT [package=kps-1290]

nets:
  3V3: D1ML1.3V3, Part5.VDD, MCP1700.OUT, C3.+, R4.Pin_0
  N1: D1ML1.5V, TP4056.pin1
  N2: D1ML1.G, TP4056.pin2
  N3: D1ML1.D4, LED2.cathode
  N4: D1ML1.D3, D1ML1.D2, Part5.ADDR, Part5.SDA
  N5: D1ML1.D1, Part5.SCL, Part5.GND
  N6: BAT1.+, U1.S
  N7: BAT1.-, TP4056.pin5
  N8: Part5.AIN3, R5.Pin_0, R6.Pin_0
  N9: R5.Pin_1, MCP1700.IN, C2.+, TP4056.pin3
  N10: R6.Pin_1, MCP1700.GND, C3.-, C2.-, TP4056.pin6
  N11: TP4056.pin4, U1.P
  N12: R4.Pin_1, LED2.anode

custom parts:
  WeMos D1 Mini Lite: A simple wifi board with 1MB flash based on ESP-8285
  18650 battery holder: 18650 Battery Holder
  Adafruit ADS1115 16Bit I2C ADC: For microcontrollers without an analog-to-digital converter or when you want a higher-precision ADC, the ADS1115 provides 16-bit precision at 860 samples/second over I2C. The chip can be configured as 4 single-ended input channels, or two differential channels. As a nice bonus, it even includes a programmable gain amplifier, up to x16, to help boost up smaller single/differential signals to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
  TP4056: A DIP stand-in part for whatever IC you want. With 6 pins on a 300mil dual inline package (DIP) footprint.
