# Fritzing sketch bridge (saved by Fritzing 0.9.9b)

parts:
  R1 = Resistor [tolerance=±5% power=0.25 resistance=330 package=THT]
  LED1 = LED - 3mm [color="Green (565nm)" current=0.030 package="3 mm [THT]"]
  U1 = ESP32-38PinWide [part_number="ESP32 (NodeMCU)"]

nets:
  N1: R1.Pin_0, LED1.anode
  N2: R1.Pin_1, U1.GPIO15
  N3: LED1.cathode, U1.GND

custom parts:
  ESP32-38PinWide: Generic 38-Pin ESP32 with wide format (only access to one side of pins on a breadboard) based on Stephen Lilley's HiLetgo ESP-WROOM-32 ESP32 ESP-32S Development Board.
